// Logisim project TriggerT.circ as structural Verilog: 1 circuit, main circuit main
module main (
  input  V,
  output q3,
  output q2,
  output q1
);

  wire and_1_out, and_2_out, clock_1_out, not_1_out, or_1_out, xor_1_out;

  xor xor_1 (xor_1_out, q1, not_1_out);
  and and_1 (and_1_out, V, q1);
  and and_2 (and_2_out, V, xor_1_out);
  not not_1 (not_1_out, q2);
  or or_1 (or_1_out, and_1_out, q1);
  Clock clock_1 (.out(clock_1_out));
  T_Flip_Flop t_ff_1 (.T(clock_1_out), .clk(and_2_out), .Q(q3));  // open: Qn, reset, preset
  T_Flip_Flop t_ff_2 (.T(clock_1_out), .clk(or_1_out), .Q(q2));  // open: Qn, reset, preset
  T_Flip_Flop t_ff_3 (.T(clock_1_out), .clk(V), .Q(q1));  // open: Qn, reset, preset

  // Notes on the sheet:
  //   h3
  //   h2
  //   h1
endmodule
